# Fritzing sketch breadboard (saved by Fritzing 0.8.7b)
breadboards: 1

parts:
  Part1 = Arduino Nano (Rev3.0)
  S2 = Momentary Switch [part_number=b package=ksa_sealed_tac_switch]
  S3 = Momentary Switch [part_number=a package=ksa_sealed_tac_switch]
  S4 = Momentary Switch [part_number=left package=ksa_sealed_tac_switch]
  S5 = Momentary Switch [part_number=right package=ksa_sealed_tac_switch]
  S6 = Momentary Switch [part_number=up package=ksa_sealed_tac_switch]
  J1 = Piezo Speaker
  S1 = Momentary Switch [part_number=down package=ksa_sealed_tac_switch]
  R4 = Resistor [tolerance=±1% resistance=10k package=THT]
  GLCD_128x1 = 128 x 64 Graphic LCD

nets:
  N1: Part1.GND, S2.1, S2.2, S3.1, S3.2, S4.1, S5.1, S6.1, S6.2, S1.1, S1.2, GLCD_128x1.1_Vss, GLCD_128x1.20_K(-)
  N2: Part1.D2, S1.3, S1.4
  N3: Part1.D3, S5.3
  N4: Part1.D4, S3.3, S3.4
  N5: Part1.D9, R4.Pin_1
  N6: Part1.D11/MOSI, GLCD_128x1.5_R/W
  N7: Part1.D12/MISO, GLCD_128x1.4_D/I
  N8: Part1.5V, GLCD_128x1.2_Vdd, GLCD_128x1.15_CS1, GLCD_128x1.19_A(+)
  N9: Part1.A3, S6.3, S6.4
  N10: Part1.A2, S2.3, S2.4
  N11: Part1.A1, S4.3
  N12: Part1.D13/SCK, GLCD_128x1.6_Enable
  N13: J1.pin2, R4.Pin_0
